# Fritzing sketch SmartShunt (saved by Fritzing 0.9.10b)
breadboards: 2

parts:
  WeMos_D1_Mini1 = WeMos D1 Mini
  J1 = Camdenboss CTB0158-3 [part_number=CTB0158-3 package=THT]  # not connected
  J2 = Camdenboss CTB0158-2 [part_number=CTB0158-2 package=THT]

nets:
  N1: WeMos_D1_Mini1.5V, J2.pin2
  N2: WeMos_D1_Mini1.G, J2.pin1
